# Fritzing sketch l298n + nema17 + arduino (saved by Fritzing 0.9.3b)

parts:
  Part1 = Arduino Nano (Rev3.0) (ICSP)
  L298N1 = L298N DC motor driver
  M1 = Stepper Motor - Bipolar
  VCC1 = Battery block 9V

nets:
  GND: Part1.GND, L298N1.GND, VCC1.-
  N1: Part1.D8, L298N1.IN1
  N2: Part1.D9, L298N1.IN2
  N3: Part1.D10, L298N1.IN3
  N4: Part1.D11/MOSI, L298N1.IN4
  N5: Part1.VIN, L298N1.5V#7
  N6: L298N1.OUT1, M1.B
  N7: L298N1.OUT2, M1.D
  N8: L298N1.OUT3, M1.C
  N9: L298N1.OUT4, M1.A
  N10: L298N1.12V, VCC1.+
  N11: L298N1.5V#9, L298N1.ENA
  N12: L298N1.5V#10, L298N1.ENB

custom parts:
  L298N DC motor driver: 2x DC motor driver with 78M05 positive voltage regulator (7..35 V) L298N: max 46 V, 2 A Set 5 V Enable jumper to enable 5 V regultor (needed for the L298N) and +5 V output at screw terminal or supply external +5 V at screw terminal Set ENA and/or ENB to +5 V to enable motor permanently or supply ENA and/or ENB with PWM signal IN1 and IN2 set rotation directory for motor A (OUT1/OUT2) IN2 and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
